// Logisim project alu.circ as structural Verilog: 1 circuit, main circuit ALU
module ALU (
  input  [7:0] A,
  input  [7:0] B,
  input  [7:0] Out,
  input  [2:0] S,
  input  ZF,
  input  VF
);

  wire adder_1_cout, and_2_out, multiplexer_3_out;
  wire [7:0] adder_1_out, and_1_out, multiplexer_1_out, multiplexer_2_out, not_1_out, not_2_out, or_1_out;

  assign not_1_out = ~B;  // NOT_Gate not_1, 8 bits wide
  Multiplexer #(.select(3), .width(8)) multiplexer_1 (
    .in0(A), .in1(B), .in2(A), .in3(B), .in4(A), .in5(A), .in6(A), .in7(A), .out(multiplexer_1_out), .sel(S));  // open: en
  Multiplexer #(.select(3), .width(8)) multiplexer_2 (
    .in0({8{1'b0}}), .in1({8{1'b0}}), .in2(8'h1), .in3(8'h1), .in4(B), .in5(not_1_out), .in6(B), .in7(B),
    .out(multiplexer_2_out), .sel(S));  // open: en
  Multiplexer #(.select(3)) multiplexer_3 (
    .in0(1'b0), .in1(1'b0), .in2(1'b0), .in3(1'b0), .in4(1'b0), .in5(1'b1), .in6(1'b0), .in7(1'b0),
    .out(multiplexer_3_out), .sel(S));  // open: en
  Adder adder_1 (
    .a(multiplexer_1_out), .b(multiplexer_2_out), .out(adder_1_out), .cin(multiplexer_3_out),
    .cout(adder_1_cout));
  assign and_1_out = multiplexer_1_out & multiplexer_2_out;  // AND_Gate and_1, 8 bits wide
  assign or_1_out = multiplexer_1_out | multiplexer_2_out;  // OR_Gate or_1, 8 bits wide
  Multiplexer #(.select(3), .width(8)) multiplexer_4 (
    .in0(adder_1_out), .in1(adder_1_out), .in2(adder_1_out), .in3(adder_1_out), .in4(adder_1_out),
    .in5(adder_1_out), .in6(and_1_out), .in7(or_1_out), .out(Out), .sel(S));  // open: en
  assign not_2_out = ~Out;  // NOT_Gate not_2, 8 bits wide
  and and_2 (and_2_out, not_2_out[7], not_2_out[6], not_2_out[5], not_2_out[4], not_2_out[3], not_2_out[2], not_2_out[1], not_2_out[0]);

  // Notes on the sheet:
  //   a+1, b+1, a+b, a-b
endmodule
